# Fritzing sketch thesis (saved by Fritzing 0.9.0b)
breadboards: 1

parts:
  Bauteil1 = Arduino Mega 2560 (Rev3)
  Bauteil2 = Arduino Board Ethernet
  U1 = mini DIN 6 Connector [package=mini-din6]
  U2 = mini DIN 6 Connector [package=mini-din6]
  R1 = Resistor [tolerance=±5% resistance=1k package=THT]
  R2 = Resistor [tolerance=±5% resistance=1k package=THT]
  R3 = Resistor [tolerance=±5% resistance=1k package=THT]

nets:
  N1: Bauteil1.D19/RX1, U2.6
  N2: Bauteil1.D18/TX1, U2.2
  N3: Bauteil1.D44, R1.Pin_0
  N4: Bauteil1.D46, R2.Pin_0
  N5: Bauteil1.D48, Bauteil2.5V, U1.3, U2.3, R3.Pin_0
  N6: Bauteil2.D2_PWM, U1.2
  N7: Bauteil2.D3_PWM, U1.6
  N8: Bauteil2.GND, U1.4, U2.4, R1.Pin_1, R2.Pin_1, R3.Pin_1
